# Fritzing sketch uno_guitar_schematic (saved by Fritzing 0.9.6b)
breadboards: 2

parts:
  R1 = Resistor [tolerance=±5% power=0.25 resistance=220 package=THT]
  R2 = Trimmer Potentiometer [maximum_resistance=10kΩ package=THT]
  JP1 = Header 3 [package=screwterminal-3.5mm-3_lock.007s]
  JP2 = Header 3 [package=screwterminal-3.5mm-3_lock.007s]
  JP3 = Header 3 [package=screwterminal-3.5mm-3_lock.007s]
  JP4 = Header 3 [package=screwterminal-3.5mm-3_lock.007s]
  JP5 = Header 3 [package=screwterminal-3.5mm-3_lock.007s]
  JP6 = Header 3 [package=screwterminal-3.5mm-3_lock.007s]
  JP7 = Header 3 [package=screwterminal-3.5mm-3_lock.007s]
  R3 = Resistor [tolerance=±5% power=0.25 resistance=220 package=THT]
  S1 = Round Pushbutton
  S2 = Round Pushbutton
  S3 = Round Pushbutton
  S4 = Round Pushbutton
  S5 = Round Pushbutton
  R4 = Resistor [tolerance=±5% power=0.25 resistance=220 package=THT]
  Part1 = Arduino Uno (Rev3)

nets:
  N1: R1.Pin_0, JP1.3, JP2.3, JP4.3, JP7.3
  N2: R1.Pin_1, JP6.2, R3.Pin_1, Part1.GND
  N3: R2.leg1, R3.Pin_0
  N4: R2.wiper, Part1.A0
  N5: R2.leg2, Part1.3V3
  N6: JP1.1, Part1.D7
  N7: JP1.2, Part1.D8
  N8: JP2.1, JP3.3, JP7.1, Part1.D11_PWM/MOSI
  N9: JP2.2, JP4.1, JP7.2, Part1.D10_PWM/SS
  N10: JP3.1, Part1.D13/SCK
  N11: JP3.2, Part1.D12/MISO
  N12: JP4.2, Part1.D9_PWM
  N13: JP5.1, JP5.2, JP5.3, JP6.1, R4.Pin_1
  N14: S1.leg0, Part1.D2
  N15: S2.leg0, Part1.D3_PWM
  N16: S3.leg0, Part1.D5_PWM
  N17: S4.leg0, Part1.D4
  N18: S5.leg1, Part1.D6_PWM
  N19: R4.Pin_0, Part1.5V

notes:
  Select / start
  stoker ( ͡° ͜ʖ ͡°)
  5(led)+3 pin
  PS/dpad 6+3-pin
  DR LR DN UP MENU GND
  whammy
